# Fritzing sketch SMARTLEDBULB (saved by Fritzing 0.9.3b)
breadboards: 1

parts:
  Part1 = Arduino Nano (Rev3.0) (ICSP)
  Part2 = Bluetooth HC-05 Macho
  LED1 = RGB LED (com. cathode, rgb) [package="5 mm [THT]"]
  U1 = Voltage Regulator - 5V [package="TO220 [THT]"]
  U2 = Voltage Regulator - 5V [package="TO220 [THT]"]
  U3 = Voltage Regulator - 5V [package="TO220 [THT]"]
  Q1 = Basic FET N-Channel [package="TO220 [THT]"]
  12V_3A = Battery Holders [package=battery-aa-panel]
  Q2 = Basic FET N-Channel [package="TO220 [THT]"]
  Q3 = Basic FET N-Channel [package="TO220 [THT]"]
  C1 = Capacitor [package=cap-pth-small]
  C4 = Capacitor [package=cap-pth-small]
  C5 = Capacitor [package=cap-pth-small]
  C6 = Capacitor [package=cap-pth-small2]
  C7 = Capacitor [package=cap-pth-small2]
  C8 = Capacitor [package=cap-pth-small2]
  R1 = Resistor [tolerance=±5% resistance=220 package="2512 [SMD]"]
  R2 = Resistor [tolerance=±5% resistance=220 package="2512 [SMD]"]
  R3 = Resistor [tolerance=±5% resistance=220 package="2512 [SMD]"]

nets:
  GND: Part1.GND, Part2.GND
  N1: Part1.D5, Part2.TXD
  N2: Part1.D6, Part2.RXD
  N3: Part1.D9, Q2.gate
  N4: Part1.D10, Q3.gate
  N5: Part1.D11/MOSI, Q1.gate
  5V: Part1.5V, Part2.VCC
  N6: LED1.red_anode, R1.Pin_1
  GND_2: LED1.common_cathode, U1.GND, U2.GND, U3.GND, 12V_3A.-, C6.2, C7.2, C8.2
  N7: LED1.green_anode, R2.Pin_1
  N8: LED1.blue_anode, R3.Pin_1
  N9: U1.input_voltage, C5.1
  N10: U1.output_voltage, Q1.source, C6.1
  N11: U2.input_voltage, C4.1
  N12: U2.output_voltage, Q3.source, C8.1
  N13: U3.input_voltage, C1.1
  N14: U3.output_voltage, Q2.source, C7.1
  N15: Q1.drain, R3.Pin_0
  N16: 12V_3A.+, C1.2, C4.2, C5.2
  N17: Q2.drain, R1.Pin_0
  N18: Q3.drain, R2.Pin_0

notes:
  MOSFET: FQP30N06L(N-channel, 60V, 32A)
  Voltage Reg.: LM7805
  Blue Capaciotr: 0.3uF
  Brown Capacitor: 0.1uF
  INPUT: 12V,3A
  RGB LED Common Cathode
